# Fritzing sketch capphoi (saved by Fritzing 0.9.3b)
breadboards: 1

parts:
  Part1 = Arduino Uno (Rev3) - ICSP
  MODE = Pushbutton [package="[SMD]"]
  DOWN = Pushbutton [package="[SMD]"]
  R1 = Resistor [tolerance=±5% resistance=10k package="1206 [SMD]"]
  R2 = Resistor [tolerance=±5% resistance=10k package="1206 [SMD]"]
  RUN = Pushbutton [package="[SMD]"]
  UP = Pushbutton [package="[SMD]"]
  R3 = Resistor [tolerance=±5% resistance=10k package="1206 [SMD]"]
  R4 = Resistor [tolerance=±5% resistance=10k package="1206 [SMD]"]
  CIRCLE = SWITCH_SPDT [package=kps-1290]
  Part2 = Jtron 1 Channel Optoisolated Relay Module [package=relay]
  Part3 = LCD1602-I2C

nets:
  N1: Part1.A0, DOWN.Pin_1, DOWN.Pin_2, R2.Pin_1
  N2: Part1.A1, MODE.Pin_1, MODE.Pin_2, R1.Pin_1
  N3: Part1.A2, UP.Pin_1, UP.Pin_2, R3.Pin_1
  N4: Part1.A3, RUN.Pin_1, RUN.Pin_2, R4.Pin_1
  N5: Part1.A4/SDA, Part3.SDA
  N6: Part1.A5/SCL, Part3.SCL
  GND: Part1.GND, R1.Pin_0, R2.Pin_0, R3.Pin_0, R4.Pin_0, CIRCLE.S, Part2.GND, Part3.GND
  N7: Part1.D12/MISO, Part2.IN1
  N8: Part1.D13/SCK, CIRCLE.P
  VCC: Part1.5V, MODE.Pin_3, MODE.Pin_4, DOWN.Pin_3, DOWN.Pin_4, RUN.Pin_3, RUN.Pin_4, UP.Pin_3, UP.Pin_4, CIRCLE.O, Part2.VCC, Part3.VCC

custom parts:
  LCD1602-I2C: A standard character display, usually with 2x16 characters. Comes in many colors with LCM1602 IIC attached.
