# Fritzing sketch Flame_Alarm (saved by Fritzing 0.9.3b)

parts:
  Part1 = Arduino Uno (Rev3)
  Mod1 = KY-026 Flame Sensor Module [package="Breakout board"]
  J1 = Piezo Speaker
  M1 = DC Motor
  KY-1 = Keyes Relay [package=THT]
  JACK1 = 2.1mm Barrel Jack with Terminal Block
  J2 = Basic Servo
  S1 = Round Pushbutton
  R1 = Temperature Sensor (Thermistor) [thermistor_type=NTC package=THT]
  R1_2 = Resistor [tolerance=±5% resistance=10k package="0402 [SMD]"]
  SIM800L1 = SIM800L
  BATT1 = LiPoly Battery (1300mAh)
  R2 = Resistor [tolerance=±5% resistance=10k package="0402 [SMD]"]
  R3 = Resistor [tolerance=±5% resistance=20k package="0402 [SMD]"]  # not connected

nets:
  N1: Part1.A0, R1.pin_0, R1_2.Pin_0
  N2: Part1.D8, J1.pin2
  N3: Part1.D9_PWM, J2.pulse
  N4: Part1.D10_PWM/SS, KY-1.signal
  N5: Part1.GND, J1.pin1
  N6: Part1.D2, R2.Pin_1
  N7: Part1.D3_PWM, SIM800L1.TXD
  N8: Part1.D4, Mod1.D0
  N9: Part1.D5_PWM, S1.leg0
  N10: Part1.5V, Mod1.+
  N11: M1.pin_1, JACK1.NEG
  N12: M1.pin_2, KY-1.NO
  N13: KY-1.C, JACK1.POS
  N14: SIM800L1.VCC, BATT1.positive
  N15: SIM800L1.RXD, R2.Pin_0
  N16: SIM800L1.GND, BATT1.negative

notes:
  1.Tracking
  - Flame = HIGH
  - or gas = HIGH
  2. Fire
  - temp > 50
  - time > 30s
  3. Pump

custom parts:
  KY-026 Flame Sensor Module: KY-026 Flame Sensor Module reacts in the presence of fire.
  Keyes Relay: The Keyes 5V relay module is suitable for SCM development, home appliance control. It uses a 5V~12V TIL control signal which can control DC / AC signal.
  SIM800L: SIM800L is a miniature cellular module which allows for GPRS transmission, sending and receiving SMS and making and receiving voice calls. Low cost and small footprint and quad band frequency support make this module perfect solution for any project that require long range connectivity. After connecting power module boots up, searches for cellular network and login automatically. On board LED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
  LiPoly Battery (1300mAh): Lithium Ion Polymer Battery (1300mAh)
