# Fritzing sketch temp_LCD_esp_ff (saved by Fritzing 0.9.3b)
breadboards: 1

parts:
  U1 = NodeMCU V1.0
  Part1 = LCD1602-I2C
  R1 = Resistor [tolerance=±5% resistance=4.7k package="2512 [SMD]"]
  LED1 = smd LED [color="Red (633nm)" package="1206 [SMD]"]
  LED2 = smd LED [color="Green (555nm)" package="1206 [SMD]"]
  J1 = Piezo Speaker
  DS1 = DS18B20 1-Wire Temperature Sensor [part_number=DS18B20]

nets:
  N1: U1.D3, R1.Pin_1, DS1.DQ
  N2: U1.D4, Part1.SDA
  GND: U1.GND, Part1.GND, LED1.cathode, LED2.cathode, J1.pin1, DS1.GND
  N3: U1.D5, Part1.SCL
  N4: U1.D6, J1.pin2
  N5: U1.D7, LED2.anode
  N6: U1.D8, LED1.anode
  VIN: U1.Vin, Part1.VCC, R1.Pin_0, DS1.VDD

custom parts:
  NodeMCU V1.0: ESP8266 based NodeMCU
  LCD1602-I2C: A standard character display, usually with 2x16 characters. Comes in many colors with LCM1602 IIC attached.
